# Fritzing sketch UselessMachine (saved by Fritzing 0.9.2b)
circuit board: 8.46667cm x 5.64444cm
breadboards: 1

parts:
  Part1 = Arduino Uno (Rev3)
  J1 = Basic Servo
  J2 = Basic Servo
  R1 = Resistor [tolerance=±5% resistance=220 package="2512 [SMD]"]
  C1 = Electrolytic Capacitor [capacitance=1000µF package="300 mil [THT, electrolytic]"]
  U1 = SWITCH-SPST-2 [package=switch-spst-vertical]

nets:
  N1: Part1.D8, J2.pulse
  N2: Part1.D10_PWM/SS, R1.Pin_0, U1.P
  GND: Part1.GND, J1.gnd, J2.gnd, R1.Pin_1, C1.-
  N3: Part1.D5_PWM, J1.pulse
  VCC: Part1.5V, J1.vcc, J2.vcc, C1.+, U1.O
